// Logisim project tarea1.circ as structural Verilog: 8 circuits, main circuit main
module deco (
  input  x1,
  input  x0,
  output y0,
  output y1,
  output y2,
  output y3,
  output y4,
  output y5,
  output y6
);

  wire not_1_out;

  not not_1 (not_1_out, x0);
  or or_1 (y1, x1, x0);
  and and_1 (y4, x1, not_1_out);

  assign y0 = x1;
  assign y2 = x0;
  assign y3 = x1;
  assign y5 = 1'b0;
  assign y6 = x1;
endmodule

module main (
  input  in_1,
  input  in_2,
  output [1:0] out_3
);

  wire deco_1_y0, deco_1_y1, deco_1_y2, deco_1_y3, deco_1_y4, deco_1_y5, deco_1_y6;
  wire [3:0] joystick_1_x, joystick_1_y;

  Joystick joystick_1 (.x(joystick_1_x), .y(joystick_1_y));
  cursor_control cursor_control_1 (.x(joystick_1_x), .y(joystick_1_y), .out_3(out_3));
  deco deco_1 (
    .y0(deco_1_y0), .y1(deco_1_y1), .y2(deco_1_y2), .y3(deco_1_y3), .y4(deco_1_y4), .y5(deco_1_y5),
    .y6(deco_1_y6), .x0(in_1), .x1(in_2));
  _7_Segment_Display u_7_segment_display_1 (
    .g(deco_1_y6), .f(deco_1_y5), .a(deco_1_y0), .b(deco_1_y1), .e(deco_1_y4), .d(deco_1_y3), .c(deco_1_y2));  // open: dp
endmodule

module DecoBlock (
  input  [1:0] I0,
  input  [1:0] I1,
  input  [1:0] I2,
  input  [1:0] I3,
  output [6:0] O0,
  output [6:0] O1,
  output [6:0] O2,
  output [6:0] O3
);

  deco deco_1 (
    .y0(O0[0]), .y1(O0[1]), .y2(O0[2]), .y3(O0[3]), .y4(O0[4]), .y5(O0[5]), .y6(O0[6]), .x0(I0[0]), .x1(I0[1]));
  deco deco_2 (
    .y0(O1[0]), .y1(O1[1]), .y2(O1[2]), .y3(O1[3]), .y4(O1[4]), .y5(O1[5]), .y6(O1[6]), .x0(I1[0]), .x1(I1[1]));
  deco deco_3 (
    .y0(O2[0]), .y1(O2[1]), .y2(O2[2]), .y3(O2[3]), .y4(O2[4]), .y5(O2[5]), .y6(O2[6]), .x0(I2[0]), .x1(I2[1]));
  deco deco_4 (
    .y0(O3[0]), .y1(O3[1]), .y2(O3[2]), .y3(O3[3]), .y4(O3[4]), .y5(O3[5]), .y6(O3[6]), .x0(I3[0]), .x1(I3[1]));
endmodule

module vicinity (
  input  [1:0] P1,
  input  [1:0] P2,
  output out_3
);

  wire and_1_out, and_2_out, and_3_out, and_4_out, and_5_out, and_6_out, and_7_out, and_8_out, not_1_out,
       not_2_out, not_3_out, not_4_out;

  not not_1 (not_1_out, P1[1]);
  not not_2 (not_2_out, P1[0]);
  not not_3 (not_3_out, P2[1]);
  not not_4 (not_4_out, P2[0]);
  and and_1 (and_1_out, not_1_out, not_2_out, not_3_out, P2[0]);
  and and_2 (and_2_out, not_1_out, not_2_out, P2[1], not_4_out);
  and and_3 (and_3_out, not_1_out, P1[0], not_3_out, not_4_out);
  and and_4 (and_4_out, not_1_out, P1[0], P2[1], P2[0]);
  and and_5 (and_5_out, P1[1], P1[0], not_3_out, P2[0]);
  or or_1 (out_3, and_1_out, and_2_out, and_3_out, and_4_out, and_5_out, and_6_out, and_7_out, and_8_out);
  and and_6 (and_6_out, P1[1], P1[0], P2[1], not_4_out);
  and and_7 (and_7_out, P1[1], not_2_out, not_3_out, not_4_out);
  and and_8 (and_8_out, P1[1], not_2_out, P2[1], P2[0]);
endmodule

module cursor_control (
  input  [3:0] y,
  input  [3:0] x,
  output [1:0] out_3
);

  wire clock_1_out, comparator_1_lt, comparator_2_gt, comparator_3_gt, comparator_4_lt;
  wire [1:0] magic_1_out_6;

  Comparator #(.width(4), .mode("unsigned")) comparator_1 (.a(y), .b(4'b0100), .lt(comparator_1_lt));  // open: gt, eq
  Comparator #(.width(4), .mode("unsigned")) comparator_2 (.a(y), .b(4'b1100), .gt(comparator_2_gt));  // open: eq, lt
  Comparator #(.width(4), .mode("unsigned")) comparator_3 (.a(x), .b(4'b1100), .gt(comparator_3_gt));  // open: eq, lt
  Comparator #(.width(4), .mode("unsigned")) comparator_4 (.a(x), .b(4'b0100), .lt(comparator_4_lt));  // open: gt, eq
  magic magic_1 (
    .x3(comparator_1_lt), .x2(comparator_2_gt), .x1(comparator_3_gt), .x0(comparator_4_lt), .q(out_3),
    .out_6(magic_1_out_6));
  Register #(.width(2)) register_1 (.D(magic_1_out_6), .Q(out_3), .clk(clock_1_out));  // open: en, clr
  Clock clock_1 (.out(clock_1_out));

  // Notes on the sheet:
  //   Up
  //   Down
  //   Right
  //   Left
endmodule

module magic_d0 (
  input  x3,
  input  x2,
  input  x1,
  input  x0,
  input  q1,
  input  q0,
  output out_7
);

  wire and_1_out, and_2_out, and_3_out, and_4_out, and_5_out, not_1_out, not_2_out, not_3_out;

  not not_1 (not_1_out, x3);
  not not_2 (not_2_out, x2);
  not not_3 (not_3_out, x0);
  and and_1 (and_1_out, not_1_out, not_2_out, x1, not_3_out);
  and and_2 (and_2_out, not_1_out, x1, x0, q0);
  and and_3 (and_3_out, x3, x0, q0);
  and and_4 (and_4_out, x2, x0, q0);
  or or_1 (out_7, and_1_out, and_2_out, and_3_out, and_4_out, and_5_out);
  and and_5 (and_5_out, not_3_out, q0);
endmodule

module magic_d1 (
  input  x3,
  input  x2,
  input  x1,
  input  x0,
  input  q1,
  input  q0,
  output out_7
);

  wire and_1_out, and_2_out, and_3_out, and_4_out, and_5_out, and_6_out, not_1_out, not_3_out, not_4_out;

  not not_1 (not_1_out, x3);
  // NOT_Gate not_2 has open pins: in=x2, out=open
  not not_3 (not_3_out, x1);
  not not_4 (not_4_out, x0);
  and and_1 (and_1_out, not_1_out, x2, not_3_out, not_4_out);
  and and_2 (and_2_out, not_1_out, x2, not_3_out, q1);
  and and_3 (and_3_out, x2, not_3_out, q1);
  and and_4 (and_4_out, x3, x1, q1);
  or or_1 (out_7, and_1_out, and_2_out, and_4_out, and_3_out, and_5_out, and_6_out);
  and and_5 (and_5_out, not_1_out, q1);
  and and_6 (and_6_out, x0, q1);
endmodule

module magic (
  input  x3,
  input  x2,
  input  x1,
  input  x0,
  input  [1:0] q,
  output [1:0] out_6
);

  magic_d1 magic_d1_1 (.x3(x3), .x2(x2), .x1(x1), .x0(x0), .q1(q[1]), .q0(q[0]), .out_7(out_6[1]));
  magic_d0 magic_d0_1 (.x3(x3), .x2(x2), .x1(x1), .x0(x0), .q1(q[1]), .q0(q[0]), .out_7(out_6[0]));
endmodule
